// Logisim project 16bitCPU.circ as structural Verilog
module _8_Bit_ALU (
  input  [7:0] A,
  input  [7:0] B,
  input  [1:0] ALU_Op,
  output [7:0] ALU_Out,
  output ZeroFlag
);

  wire and_1_out;
  wire [7:0] adder_1_out, and_2_out, multiplexer_1_out, not_1_out, or_1_out;

  Multiplexer #(.width(8), .enable("false")) multiplexer_1 (
    .in0(B), .in1(not_1_out), .out(multiplexer_1_out), .sel(and_1_out));
  assign not_1_out = ~B;  // NOT_Gate not_1, 8 bits wide
  and and_1 (and_1_out, ALU_Op[0], ALU_Op[1]);
  Adder adder_1 (.a(A), .b(multiplexer_1_out), .out(adder_1_out), .cin(and_1_out));  // open: cout
  assign and_2_out = multiplexer_1_out & A;  // AND_Gate and_2, 8 bits wide
  assign or_1_out = multiplexer_1_out | A;  // OR_Gate or_1, 8 bits wide
  Multiplexer #(.select(2), .width(8), .enable("false")) multiplexer_2 (
    .in0(adder_1_out), .in1(and_2_out), .in2(or_1_out), .in3(adder_1_out), .out(ALU_Out), .sel(ALU_Op));
  Comparator comparator_1 (.a(ALU_Out), .b({8{1'b0}}), .eq(ZeroFlag));  // open: gt, lt

  // Notes on the sheet:
  //   8 Bit ALU
  //   00 = ADD
  //   01 = AND
  //   10 = OR
  //   11 = SUB
  //   sub not B
  //   sub cin
  //   sub
endmodule

module _16x8_bit_Register_File (
  input  [7:0] Data_In,
  input  [3:0] Read_Addr_1,
  input  Write_Enable,
  input  [3:0] Write_Addr,
  input  [3:0] Read_Addr_2,
  input  Clock,
  output [7:0] Read_1_Data,
  output [7:0] Read_2_Data
);

  wire demultiplexer_1_out0, demultiplexer_1_out1, demultiplexer_1_out2, demultiplexer_1_out3,
       demultiplexer_1_out4, demultiplexer_1_out5, demultiplexer_1_out6, demultiplexer_1_out7,
       demultiplexer_1_out8, demultiplexer_1_out9, demultiplexer_1_out10, demultiplexer_1_out11,
       demultiplexer_1_out12, demultiplexer_1_out13, demultiplexer_1_out14, demultiplexer_1_out15;
  wire [7:0] register_1_q, register_2_q, register_3_q, register_4_q, register_5_q, register_6_q,
       register_7_q, register_8_q, register_9_q, register_10_q, register_11_q, register_12_q, register_13_q,
       register_14_q, register_15_q, register_16_q;

  Demultiplexer #(.select(4), .enable("false")) demultiplexer_1 (
    .out0(demultiplexer_1_out0), .out1(demultiplexer_1_out1), .out2(demultiplexer_1_out2),
    .out3(demultiplexer_1_out3), .out4(demultiplexer_1_out4), .out5(demultiplexer_1_out5),
    .out6(demultiplexer_1_out6), .out7(demultiplexer_1_out7), .out8(demultiplexer_1_out8),
    .out9(demultiplexer_1_out9), .out10(demultiplexer_1_out10), .out11(demultiplexer_1_out11),
    .out12(demultiplexer_1_out12), .out13(demultiplexer_1_out13), .out14(demultiplexer_1_out14),
    .out15(demultiplexer_1_out15), .in(Write_Enable), .sel(Write_Addr));
  Register register_1 (.D(Data_In), .en(demultiplexer_1_out0), .Q(register_1_q), .clk(Clock));  // open: clr
  Register register_2 (.D(Data_In), .en(demultiplexer_1_out1), .Q(register_2_q), .clk(Clock));  // open: clr
  Register register_3 (.D(Data_In), .en(demultiplexer_1_out2), .Q(register_3_q), .clk(Clock));  // open: clr
  Register register_4 (.D(Data_In), .en(demultiplexer_1_out3), .Q(register_4_q), .clk(Clock));  // open: clr
  Register register_5 (.D(Data_In), .en(demultiplexer_1_out4), .Q(register_5_q), .clk(Clock));  // open: clr
  Register register_6 (.D(Data_In), .en(demultiplexer_1_out5), .Q(register_6_q), .clk(Clock));  // open: clr
  Register register_7 (.D(Data_In), .en(demultiplexer_1_out6), .Q(register_7_q), .clk(Clock));  // open: clr
  Register register_8 (.D(Data_In), .en(demultiplexer_1_out7), .Q(register_8_q), .clk(Clock));  // open: clr
  Register register_9 (.D(Data_In), .en(demultiplexer_1_out8), .Q(register_9_q), .clk(Clock));  // open: clr
  Register register_10 (.D(Data_In), .en(demultiplexer_1_out9), .Q(register_10_q), .clk(Clock));  // open: clr
  Register register_11 (.D(Data_In), .en(demultiplexer_1_out10), .Q(register_11_q), .clk(Clock));  // open: clr
  Register register_12 (.D(Data_In), .en(demultiplexer_1_out11), .Q(register_12_q), .clk(Clock));  // open: clr
  Register register_13 (.D(Data_In), .en(demultiplexer_1_out12), .Q(register_13_q), .clk(Clock));  // open: clr
  Register register_14 (.D(Data_In), .en(demultiplexer_1_out13), .Q(register_14_q), .clk(Clock));  // open: clr
  Register register_15 (.D(Data_In), .en(demultiplexer_1_out14), .Q(register_15_q), .clk(Clock));  // open: clr
  Register register_16 (.D(Data_In), .en(demultiplexer_1_out15), .Q(register_16_q), .clr(Clock));  // open: clk
  Multiplexer #(.select(4), .width(8), .enable("false")) multiplexer_1 (
    .in0(register_1_q), .in1(register_2_q), .in2(register_3_q), .in3(register_4_q), .in4(register_5_q),
    .in5(register_6_q), .in6(register_7_q), .in7(register_8_q), .in8(register_9_q), .in9(register_10_q),
    .in10(register_11_q), .in11(register_12_q), .in12(register_13_q), .in13(register_14_q),
    .in14(register_15_q), .in15(register_16_q), .out(Read_1_Data), .sel(Read_Addr_1));
  Multiplexer #(.select(4), .width(8), .enable("false")) multiplexer_2 (
    .in0(register_1_q), .in1(register_2_q), .in2(register_3_q), .in3(register_4_q), .in4(register_5_q),
    .in5(register_6_q), .in6(register_7_q), .in7(register_8_q), .in8(register_9_q), .in9(register_10_q),
    .in10(register_11_q), .in11(register_12_q), .in12(register_13_q), .in13(register_14_q),
    .in14(register_15_q), .in15(register_16_q), .out(Read_2_Data), .sel(Read_Addr_2));

  // Notes on the sheet:
  //   16x8-bit Register File
endmodule

module PC (
  input  [7:0] in_1,
  input  CLK,
  input  Reset,
  output [7:0] Out
);

  wire [7:0] ALU_alu_out;

  Register Register (.D(ALU_alu_out), .en(1'b1), .Q(Out), .clk(CLK), .clr(Reset));
  _8_Bit_ALU ALU (.A(Out), .B(in_1), .ALU_Op(2'b00), .ALU_Out(ALU_alu_out));  // open: ZeroFlag
endmodule

module CLUasLookupTable (
  input  [3:0] opcode,
  output Beq,
  output J,
  output LW,
  output SW,
  output WE,
  output [1:0] ALUop,
  output IMM
);

  ROM #(.addrWidth(4)) rom_1 (.addr(opcode), .data({IMM, ALUop, WE, SW, LW, J, Beq}), .sel(1'b1));

  // Notes on the sheet:
  //   contents of rom_1 (hex, n*v repeats v):
  //   10 20 50 70 4*0 90 b0 d0 f0 94 88 61 82
endmodule

module Basic16bitCPU (
  input  CLK,
  input  Reset,
  output [7:0] CPU_Op_Out,
  output [7:0] out_4
);

  wire cluaslookuptable_1_imm, LW, SW, WE;
  wire [1:0] cluaslookuptable_1_aluop;
  wire [3:0] multiplexer_1_out;
  wire [7:0] ALU_read_1_data, ALU_read_2_data, bit_extender_1_out, multiplexer_2_out, multiplexer_3_out,
       ram_2_data;
  wire [15:0] ram_1_data;

  PC PC (.in_1(8'h1), .CLK(CLK), .Reset(Reset), .Out(out_4));
  RAM #(.dataWidth(16)) ram_1 (.addr(out_4), .data(ram_1_data), .sel(1'b1), .ld(1'b1), .clr(1'b0));  // open: clk
  CLUasLookupTable cluaslookuptable_1 (
    .opcode(ram_1_data[15:12]), .LW(LW), .SW(SW), .WE(WE), .ALUop(cluaslookuptable_1_aluop),
    .IMM(cluaslookuptable_1_imm));  // open: Beq, J
  _16x8_bit_Register_File ALU (
    .Data_In(multiplexer_3_out), .Write_Enable(WE), .Clock(CLK), .Write_Addr(ram_1_data[3:0]),
    .Read_Addr_1(ram_1_data[11:8]), .Read_Addr_2(multiplexer_1_out), .Read_1_Data(ALU_read_1_data),
    .Read_2_Data(ALU_read_2_data));
  Multiplexer #(.width(4), .enable("false")) multiplexer_1 (
    .in0(ram_1_data[7:4]), .in1(ram_1_data[3:0]), .out(multiplexer_1_out), .sel(SW));
  assign bit_extender_1_out = {{4{ram_1_data[7]}}, ram_1_data[7:4]};  // Bit_Extender bit_extender_1
  Multiplexer #(.width(8), .enable("false")) multiplexer_2 (
    .in0(ALU_read_2_data), .in1(bit_extender_1_out), .out(multiplexer_2_out), .sel(cluaslookuptable_1_imm));
  Multiplexer #(.width(8), .enable("false")) multiplexer_3 (
    .in0(CPU_Op_Out), .in1(ram_2_data), .out(multiplexer_3_out), .sel(LW));
  _8_Bit_ALU ALU_2 (
    .A(ALU_read_1_data), .B(multiplexer_2_out), .ALU_Op(cluaslookuptable_1_aluop), .ALU_Out(CPU_Op_Out));  // open: ZeroFlag
  RAM #(.bus("separate")) ram_2 (
    .addr(CPU_Op_Out), .din(ALU_read_2_data), .data(ram_2_data), .str(SW), .sel(1'b1), .clk(CLK), .ld(LW),
    .clr(1'b0));

  // Notes on the sheet:
  //   Instr Memory
  //   dest
  //   src2
  //   src1
  //   op
  //   immed data
  //   RAM
endmodule

module PC2 (
  input  [7:0] in,
  input  CLK,
  input  Reset,
  output [7:0] Out
);

  Register Register (.D(in), .en(1'b1), .Q(Out), .clk(CLK), .clr(Reset));
endmodule

module _16bitCPUwithBeq (
  input  CLK,
  input  Reset,
  output [7:0] CPU_Op_Out,
  output [7:0] out_4
);

  wire ALU_2_zeroflag, and_1_out, beq, cluaslookuptable_1_imm, LW, or_1_out, SW, WE;
  wire [1:0] cluaslookuptable_1_aluop;
  wire [3:0] multiplexer_2_out;
  wire [7:0] adder_1_out, ALU_read_1_data, ALU_read_2_data, bit_extender_1_out, multiplexer_1_out,
       multiplexer_3_out, multiplexer_4_out, ram_2_data;
  wire [15:0] ram_1_data;

  Multiplexer #(.width(8), .enable("false")) multiplexer_1 (
    .in0(8'h1), .in1(adder_1_out), .out(multiplexer_1_out), .sel(and_1_out));
  PC PC (.in_1(multiplexer_1_out), .CLK(CLK), .Reset(Reset), .Out(out_4));
  RAM #(.dataWidth(16)) ram_1 (.addr(out_4), .data(ram_1_data), .sel(1'b1), .ld(1'b1), .clr(1'b0));  // open: clk
  CLUasLookupTable cluaslookuptable_1 (
    .opcode(ram_1_data[15:12]), .Beq(beq), .LW(LW), .SW(SW), .WE(WE), .ALUop(cluaslookuptable_1_aluop),
    .IMM(cluaslookuptable_1_imm));  // open: J
  Multiplexer #(.width(4), .enable("false")) multiplexer_2 (
    .in0(ram_1_data[7:4]), .in1(ram_1_data[3:0]), .out(multiplexer_2_out), .sel(or_1_out));
  or or_1 (or_1_out, beq, SW);
  _16x8_bit_Register_File ALU (
    .Data_In(multiplexer_4_out), .Write_Enable(WE), .Clock(CLK), .Write_Addr(ram_1_data[3:0]),
    .Read_Addr_1(ram_1_data[11:8]), .Read_Addr_2(multiplexer_2_out), .Read_1_Data(ALU_read_1_data),
    .Read_2_Data(ALU_read_2_data));
  Multiplexer #(.width(8), .enable("false")) multiplexer_3 (
    .in0(ALU_read_2_data), .in1(bit_extender_1_out), .out(multiplexer_3_out), .sel(cluaslookuptable_1_imm));
  assign bit_extender_1_out = {{4{ram_1_data[7]}}, ram_1_data[7:4]};  // Bit_Extender bit_extender_1
  Multiplexer #(.width(8), .enable("false")) multiplexer_4 (
    .in0(CPU_Op_Out), .in1(ram_2_data), .out(multiplexer_4_out), .sel(LW));
  _8_Bit_ALU ALU_2 (
    .A(ALU_read_1_data), .B(multiplexer_3_out), .ALU_Op(cluaslookuptable_1_aluop), .ALU_Out(CPU_Op_Out),
    .ZeroFlag(ALU_2_zeroflag));
  Adder adder_1 (.a(bit_extender_1_out), .b(8'h1), .out(adder_1_out));  // open: cin, cout
  and and_1 (and_1_out, beq, ALU_2_zeroflag);
  RAM #(.bus("separate")) ram_2 (
    .addr(CPU_Op_Out), .din(ALU_read_2_data), .data(ram_2_data), .str(SW), .sel(1'b1), .clk(CLK), .ld(LW),
    .clr(1'b0));

  // Notes on the sheet:
  //   Instr Memory
  //   dest
  //   src2
  //   src1
  //   op
  //   immed data
  //   RAM
endmodule

module _16bitCPUwithJump (
  input  CLK,
  input  Reset,
  output [7:0] CPU_Op_Out,
  output [7:0] out_4
);

  wire ALU_zeroflag, and_1_out, beq, cluaslookuptable_1_imm, J, LW, or_1_out, SW, WE;
  wire [1:0] cluaslookuptable_1_aluop;
  wire [3:0] multiplexer_3_out;
  wire [7:0] adder_1_out, adder_2_out, bit_extender_1_out, multiplexer_1_out, multiplexer_2_out,
       multiplexer_4_out, multiplexer_5_out, n16x8_bit_register_file_1_read_1_data,
       n16x8_bit_register_file_1_read_2_data, ram_1_data, ram_2_data;
  wire [15:8] ram_1_data_2;

  Multiplexer #(.width(8), .enable("false")) multiplexer_1 (
    .in0(adder_1_out), .in1(adder_2_out), .out(multiplexer_1_out), .sel(and_1_out));
  Multiplexer #(.width(8), .enable("false")) multiplexer_2 (
    .in0(multiplexer_1_out), .in1(ram_1_data), .out(multiplexer_2_out), .sel(J));
  PC2 PC2 (.in(multiplexer_2_out), .CLK(CLK), .Reset(Reset), .Out(out_4));
  Adder adder_1 (.a(out_4), .b(8'h1), .out(adder_1_out));  // open: cin, cout
  RAM #(.dataWidth(16)) ram_1 (
    .addr(out_4), .data({ram_1_data_2, ram_1_data}), .sel(1'b1), .ld(1'b1), .clr(1'b0));  // open: clk
  CLUasLookupTable cluaslookuptable_1 (
    .opcode(ram_1_data_2[15:12]), .Beq(beq), .J(J), .LW(LW), .SW(SW), .WE(WE),
    .ALUop(cluaslookuptable_1_aluop), .IMM(cluaslookuptable_1_imm));
  _16x8_bit_Register_File u_16x8_bit_register_file_1 (
    .Data_In(multiplexer_5_out), .Write_Enable(WE), .Clock(CLK), .Write_Addr(ram_1_data[3:0]),
    .Read_Addr_1(ram_1_data_2[11:8]), .Read_Addr_2(multiplexer_3_out),
    .Read_1_Data(n16x8_bit_register_file_1_read_1_data), .Read_2_Data(n16x8_bit_register_file_1_read_2_data));
  Multiplexer #(.width(4), .enable("false")) multiplexer_3 (
    .in0(ram_1_data[7:4]), .in1(ram_1_data[3:0]), .out(multiplexer_3_out), .sel(or_1_out));
  or or_1 (or_1_out, beq, SW);
  Multiplexer #(.width(8), .enable("false")) multiplexer_4 (
    .in0(n16x8_bit_register_file_1_read_2_data), .in1(bit_extender_1_out), .out(multiplexer_4_out),
    .sel(cluaslookuptable_1_imm));
  assign bit_extender_1_out = {{4{ram_1_data[7]}}, ram_1_data[7:4]};  // Bit_Extender bit_extender_1
  Multiplexer #(.width(8), .enable("false")) multiplexer_5 (
    .in0(CPU_Op_Out), .in1(ram_2_data), .out(multiplexer_5_out), .sel(LW));
  _8_Bit_ALU ALU (
    .A(n16x8_bit_register_file_1_read_1_data), .B(multiplexer_4_out), .ALU_Op(cluaslookuptable_1_aluop),
    .ALU_Out(CPU_Op_Out), .ZeroFlag(ALU_zeroflag));
  Adder adder_2 (.a(bit_extender_1_out), .b(adder_1_out), .out(adder_2_out));  // open: cin, cout
  and and_1 (and_1_out, beq, ALU_zeroflag);
  RAM #(.bus("separate")) ram_2 (
    .addr(CPU_Op_Out), .din(n16x8_bit_register_file_1_read_2_data), .data(ram_2_data), .str(SW), .sel(1'b1),
    .clk(CLK), .ld(LW), .clr(1'b0));

  // Notes on the sheet:
  //   Instr Memory
  //   src2
  //   src1
  //   dest
  //   op
  //   immed data
  //   RAM
endmodule
